# Fritzing sketch pcb (saved by Fritzing 0.9.3b)
circuit board: 15.24cm x 15.24cm
breadboards: 1

parts:
  J5 = female pin header, 8 pins [form="♀ (female)"]
  J6 = female pin header, 8 pins [form="♀ (female)"]
  JP2 = Header 5x2 [package=avr_icsp]
  J7 = male pin header, 10 pins [form="♂ (male)"]
  J8 = male pin header, 10 pins [form="♂ (male)"]
  Pro_Micro1 = SparkFun Pro Micro
  JP5 = Header 5x2 [package=avr_icsp]
  J17 = female pin header, 8 pins [form="♀ (female)"]
  J18 = male pin header, 16 pins [form="♂ (male)"]
  J19 = female pin header, 8 pins [form="♀ (female)"]
  J20 = male pin header, 16 pins [form="♂ (male)"]
  J21 = female pin header, 8 pins [form="♀ (female)"]
  J22 = female pin header, 8 pins [form="♀ (female)"]
  JP6 = Header 5x2 [package=avr_icsp]
  J23 = male pin header, 10 pins [form="♂ (male)"]
  J24 = male pin header, 10 pins [form="♂ (male)"]
  J25 = female pin header, 8 pins [form="♀ (female)"]
  J26 = male pin header, 16 pins [form="♂ (male)"]
  J27 = female pin header, 8 pins [form="♀ (female)"]
  J28 = female pin header, 8 pins [form="♀ (female)"]
  JP7 = Header 5x2 [package=avr_icsp]
  J29 = male pin header, 10 pins [form="♂ (male)"]
  J30 = male pin header, 10 pins [form="♂ (male)"]
  J31 = female pin header, 8 pins [form="♀ (female)"]
  J32 = male pin header, 16 pins [form="♂ (male)"]
  J33 = female pin header, 8 pins [form="♀ (female)"]
  J34 = female pin header, 8 pins [form="♀ (female)"]
  JP8 = Header 5x2 [package=avr_icsp]
  J35 = male pin header, 10 pins [form="♂ (male)"]
  J36 = male pin header, 10 pins [form="♂ (male)"]
  C1 = Ceramic Capacitor [capacitance=100nF package="100 mil [THT, multilayer]"]
  C2 = Ceramic Capacitor [capacitance=100nF package="100 mil [THT, multilayer]"]
  C3 = Ceramic Capacitor [capacitance=100nF package="100 mil [THT, multilayer]"]
  0_1uF = Ceramic Capacitor [capacitance=100nF package="100 mil [THT, multilayer]"]
  J44 = female pin header, 5 pins [form="♀ (female)"]
  J45 = female pin header, 4 pins [form="♀ (female)"]  # not connected
  J46 = female pin header, 2 pins [form="♀ (female)"]
  J47 = female pin header, 2 pins [form="♀ (female)"]
  J48 = female pin header, 5 pins [form="♀ (female)"]
  J49 = female pin header, 2 pins [form="♀ (female)"]
  J50 = female pin header, 4 pins [form="♀ (female)"]
  J51 = female pin header, 5 pins [form="♀ (female)"]
  J52 = female pin header, 4 pins [form="♀ (female)"]  # not connected
  J53 = female pin header, 2 pins [form="♀ (female)"]
  J54 = female pin header, 2 pins [form="♀ (female)"]
  J55 = female pin header, 5 pins [form="♀ (female)"]
  J56 = female pin header, 2 pins [form="♀ (female)"]
  J57 = female pin header, 4 pins [form="♀ (female)"]
  J58 = female pin header, 5 pins [form="♀ (female)"]
  J59 = female pin header, 4 pins [form="♀ (female)"]  # not connected
  J60 = female pin header, 2 pins [form="♀ (female)"]
  J61 = female pin header, 2 pins [form="♀ (female)"]
  J62 = female pin header, 5 pins [form="♀ (female)"]
  J63 = female pin header, 2 pins [form="♀ (female)"]
  J64 = female pin header, 4 pins [form="♀ (female)"]
  J65 = female pin header, 5 pins [form="♀ (female)"]
  J66 = female pin header, 4 pins [form="♀ (female)"]  # not connected
  J67 = female pin header, 2 pins [form="♀ (female)"]
  J68 = female pin header, 2 pins [form="♀ (female)"]
  J69 = female pin header, 5 pins [form="♀ (female)"]
  J70 = female pin header, 2 pins [form="♀ (female)"]
  J71 = female pin header, 4 pins [form="♀ (female)"]
  J72 = female pin header, 5 pins [form="♀ (female)"]
  J73 = female pin header, 4 pins [form="♀ (female)"]  # not connected
  J74 = female pin header, 2 pins [form="♀ (female)"]
  J75 = female pin header, 2 pins [form="♀ (female)"]
  J76 = female pin header, 5 pins [form="♀ (female)"]
  J77 = female pin header, 2 pins [form="♀ (female)"]
  J78 = female pin header, 4 pins [form="♀ (female)"]
  J79 = female pin header, 4 pins [form="♀ (female)"]  # not connected
  J80 = female pin header, 5 pins [form="♀ (female)"]
  J81 = female pin header, 2 pins [form="♀ (female)"]
  J82 = female pin header, 2 pins [form="♀ (female)"]
  J83 = female pin header, 5 pins [form="♀ (female)"]
  J84 = female pin header, 4 pins [form="♀ (female)"]
  J85 = female pin header, 2 pins [form="♀ (female)"]
  J86 = female pin header, 2 pins [form="♀ (female)"]
  J87 = female pin header, 5 pins [form="♀ (female)"]
  J88 = female pin header, 4 pins [form="♀ (female)"]
  J89 = female pin header, 5 pins [form="♀ (female)"]
  J90 = female pin header, 4 pins [form="♀ (female)"]  # not connected
  J91 = female pin header, 2 pins [form="♀ (female)"]
  J92 = female pin header, 2 pins [form="♀ (female)"]
  J93 = female pin header, 2 pins [form="♀ (female)"]
  J94 = female pin header, 5 pins [form="♀ (female)"]
  J95 = female pin header, 4 pins [form="♀ (female)"]
  J96 = female pin header, 5 pins [form="♀ (female)"]
  J97 = female pin header, 4 pins [form="♀ (female)"]  # not connected
  J98 = female pin header, 2 pins [form="♀ (female)"]
  J99 = female pin header, 2 pins [form="♀ (female)"]
  J100 = female pin header, 2 pins [form="♀ (female)"]
  J101 = female pin header, 5 pins [form="♀ (female)"]
  J102 = female pin header, 4 pins [form="♀ (female)"]
  J103 = female pin header, 5 pins [form="♀ (female)"]
  J104 = female pin header, 4 pins [form="♀ (female)"]  # not connected
  J105 = female pin header, 2 pins [form="♀ (female)"]
  J106 = female pin header, 2 pins [form="♀ (female)"]

nets:
  N1: J5.pin1, J18.pin2
  N2: J5.pin2, J18.pin1
  N3: J5.pin3, J18.pin3
  N4: J5.pin4, J18.pin4
  N5: J5.pin5, J18.pin5
  N6: J5.pin6, J18.pin6
  N7: J5.pin7, J18.pin7
  N8: J5.pin8, J18.pin8
  N9: J6.pin1, J18.pin15
  N10: J6.pin2, J18.pin16
  N11: J6.pin3, J18.pin14
  N12: J6.pin4, J18.pin13
  N13: J6.pin5, J18.pin12
  N14: J6.pin6, J18.pin11
  N15: J6.pin7, J18.pin10
  N16: J6.pin8, J18.pin9
  N17: JP2.1, J8.pin1, J8.pin2, J8.pin3, J8.pin4, J8.pin5, J8.pin6, J8.pin7, J8.pin8, J8.pin9, J8.pin10, 0_1uF.0
  N18: JP2.2, J7.pin1, J7.pin2, J7.pin3, J7.pin4, J7.pin5, J7.pin6, J7.pin7, J7.pin8, J7.pin9, J7.pin10, J17.pin2, 0_1uF.1
  N19: JP2.4, J17.pin4
  N20: JP2.6, J17.pin5
  N21: JP2.8, J17.pin6
  N22: JP2.9, J17.pin8
  N23: JP2.10, J17.pin7
  N24: Pro_Micro1.10, JP5.10
  N25: Pro_Micro1.16, JP5.8
  N26: Pro_Micro1.14, JP5.6
  N27: Pro_Micro1.15, JP5.4
  N28: Pro_Micro1.A0, JP5.9
  N29: Pro_Micro1.A1, JP5.7
  N30: Pro_Micro1.A2, JP5.5
  N31: Pro_Micro1.A3, JP5.3
  N32: Pro_Micro1.VCC, JP5.2
  N33: J19.pin2, JP6.2, J23.pin1, J23.pin2, J23.pin3, J23.pin4, J23.pin5, J23.pin6, J23.pin7, J23.pin8, J23.pin9, J23.pin10, C1.1
  N34: J19.pin4, JP6.4
  N35: J19.pin5, JP6.6
  N36: J19.pin6, JP6.8
  N37: J19.pin7, JP6.10
  N38: J19.pin8, JP6.7
  N39: J20.pin1, J22.pin2
  N40: J20.pin2, J22.pin1
  N41: J20.pin3, J22.pin3
  N42: J20.pin4, J22.pin4
  N43: J20.pin5, J22.pin5
  N44: J20.pin6, J22.pin6
  N45: J20.pin7, J22.pin7
  N46: J20.pin8, J22.pin8
  N47: J20.pin9, J21.pin8
  N48: J20.pin10, J21.pin7
  N49: J20.pin11, J21.pin6
  N50: J20.pin12, J21.pin5
  N51: J20.pin13, J21.pin4
  N52: J20.pin14, J21.pin3
  N53: J20.pin15, J21.pin1
  N54: J20.pin16, J21.pin2
  N55: JP6.1, J24.pin1, J24.pin2, J24.pin3, J24.pin4, J24.pin5, J24.pin6, J24.pin7, J24.pin8, J24.pin9, J24.pin10, C1.0
  N56: J25.pin2, JP7.2, J29.pin1, J29.pin2, J29.pin3, J29.pin4, J29.pin5, J29.pin6, J29.pin7, J29.pin8, J29.pin9, J29.pin10, C2.1
  N57: J25.pin4, JP7.4
  N58: J25.pin5, JP7.6
  N59: J25.pin6, JP7.8
  N60: J25.pin7, JP7.10
  N61: J25.pin8, JP7.3
  N62: J26.pin1, J28.pin2
  N63: J26.pin2, J28.pin1
  N64: J26.pin3, J28.pin3
  N65: J26.pin4, J28.pin4
  N66: J26.pin5, J28.pin5
  N67: J26.pin6, J28.pin6
  N68: J26.pin7, J28.pin7
  N69: J26.pin8, J28.pin8
  N70: J26.pin9, J27.pin8
  N71: J26.pin10, J27.pin7
  N72: J26.pin11, J27.pin6
  N73: J26.pin12, J27.pin5
  N74: J26.pin13, J27.pin4
  N75: J26.pin14, J27.pin3
  N76: J26.pin15, J27.pin1
  N77: J26.pin16, J27.pin2
  N78: JP7.1, J30.pin1, J30.pin2, J30.pin3, J30.pin4, J30.pin5, J30.pin6, J30.pin7, J30.pin8, J30.pin9, J30.pin10, C2.0
  N79: J31.pin2, JP8.2, J35.pin1, J35.pin2, J35.pin3, J35.pin4, J35.pin5, J35.pin6, J35.pin7, J35.pin8, J35.pin9, J35.pin10, C3.1
  N80: J31.pin4, JP8.4
  N81: J31.pin5, JP8.6
  N82: J31.pin6, JP8.8
  N83: J31.pin7, JP8.10
  N84: J31.pin8, JP8.5
  N85: J32.pin1, J34.pin2
  N86: J32.pin2, J34.pin1
  N87: J32.pin3, J34.pin3
  N88: J32.pin4, J34.pin4
  N89: J32.pin5, J34.pin5
  N90: J32.pin6, J34.pin6
  N91: J32.pin7, J34.pin7
  N92: J32.pin8, J34.pin8
  N93: J32.pin9, J33.pin8
  N94: J32.pin10, J33.pin7
  N95: J32.pin11, J33.pin6
  N96: J32.pin12, J33.pin5
  N97: J32.pin13, J33.pin4
  N98: J32.pin14, J33.pin3
  N99: J32.pin15, J33.pin1
  N100: J32.pin16, J33.pin2
  N101: JP8.1, J36.pin1, J36.pin2, J36.pin3, J36.pin4, J36.pin5, J36.pin6, J36.pin7, J36.pin8, J36.pin9, J36.pin10, C3.0
  N102: J44.pin1, J49.pin1, J50.pin1, J50.pin2, J50.pin3, J50.pin4
  N103: J44.pin3, J48.pin3
  N104: J46.pin1, J48.pin4
  N105: J46.pin2, J48.pin5
  N106: J47.pin1, J48.pin1
  N107: J47.pin2, J48.pin2
  N108: J51.pin1, J56.pin1, J57.pin1, J57.pin2, J57.pin3, J57.pin4
  N109: J51.pin3, J55.pin3
  N110: J53.pin1, J55.pin4
  N111: J53.pin2, J55.pin5
  N112: J54.pin1, J55.pin1
  N113: J54.pin2, J55.pin2
  N114: J58.pin1, J63.pin1, J64.pin1, J64.pin2, J64.pin3, J64.pin4
  N115: J58.pin3, J62.pin3
  N116: J60.pin1, J62.pin4
  N117: J60.pin2, J62.pin5
  N118: J61.pin1, J62.pin1
  N119: J61.pin2, J62.pin2
  N120: J65.pin1, J70.pin1, J71.pin1, J71.pin2, J71.pin3, J71.pin4
  N121: J65.pin3, J69.pin3
  N122: J67.pin1, J69.pin4
  N123: J67.pin2, J69.pin5
  N124: J68.pin1, J69.pin1
  N125: J68.pin2, J69.pin2
  N126: J72.pin1, J77.pin1, J78.pin1, J78.pin2, J78.pin3, J78.pin4
  N127: J72.pin3, J76.pin3
  N128: J74.pin1, J76.pin4
  N129: J74.pin2, J76.pin5
  N130: J75.pin1, J76.pin1
  N131: J75.pin2, J76.pin2
  N132: J80.pin1, J82.pin1
  N133: J80.pin2, J82.pin2
  N134: J80.pin3, J83.pin3
  N135: J80.pin4, J85.pin1
  N136: J80.pin5, J85.pin2
  N137: J81.pin1, J83.pin1, J84.pin1, J84.pin2, J84.pin3, J84.pin4
  N138: J86.pin1, J87.pin4
  N139: J86.pin2, J87.pin5
  N140: J87.pin1, J91.pin1
  N141: J87.pin2, J91.pin2
  N142: J87.pin3, J89.pin3
  N143: J88.pin1, J88.pin2, J88.pin3, J88.pin4, J89.pin1, J92.pin1
  N144: J93.pin1, J94.pin4
  N145: J93.pin2, J94.pin5
  N146: J94.pin1, J98.pin1
  N147: J94.pin2, J98.pin2
  N148: J94.pin3, J96.pin3
  N149: J95.pin1, J95.pin2, J95.pin3, J95.pin4, J96.pin1, J99.pin1
  N150: J100.pin1, J101.pin4
  N151: J100.pin2, J101.pin5
  N152: J101.pin1, J105.pin1
  N153: J101.pin2, J105.pin2
  N154: J101.pin3, J103.pin3
  N155: J102.pin1, J102.pin2, J102.pin3, J102.pin4, J103.pin1, J106.pin1

custom parts:
  SparkFun Pro Micro: The Pro Micro is similar to the Pro Mini except with an ATmega32U4 on board. The USB transceiver inside the 32U4 allows us to add USB connectivity on-board and do away with bulky external USB interface. Based on: https://github.com/unorthodox-engineers/unorthodox-arduino/blob/master/Unorthodox/fritzing/parts/Pro%20Micro.fzpz
